# Fritzing sketch diagram (saved by Fritzing 0.9.10b)

parts:
  Part1 = Arduino Uno (Rev3)
  LCD2004-I2C1 = LCD2004-I2C
  ZS-042_RTC1 = ZS-042 RTC Module
  microSD1 = MicroSD Card Module
  BAT1 = 18650 battery holder [package=battery-18650-kit]  # not connected
  BAT2 = 18650 battery holder [package=battery-18650-kit]  # not connected
  BAT3 = 18650 battery holder [package=battery-18650-kit]  # not connected
  BAT4 = 18650 battery holder [package=battery-18650-kit]  # not connected
  Mod1 = Voltage Sensor 25V
  Part2 = ACS712 Current Sensor 5A 20A 30A
  J1 = female pin header, 2 pins [form="♀ (female)"]
  J2 = female pin header, 2 pins [form="♀ (female)"]
  J3 = female pin header, 2 pins [form="♀ (female)"]
  J4 = female pin header, 2 pins [form="♀ (female)"]
  J5 = female pin header, 2 pins [form="♀ (female)"]
  J6 = female pin header, 2 pins [form="♀ (female)"]
  J7 = female pin header, 2 pins [form="♀ (female)"]

nets:
  N1: Part1.A0, Part2.2, Part2.OUT
  N2: Part1.A1, Mod1.S
  N3: Part1.D10_PWM/SS, microSD1.CS
  N4: Part1.D11_PWM/MOSI, microSD1.MOSI
  N5: Part1.D12/MISO, microSD1.MISO
  N6: Part1.D13/SCK, microSD1.SCK
  N7: LCD2004-I2C1.GND, J2.pin1
  N8: LCD2004-I2C1.VCC, J2.pin2
  N9: LCD2004-I2C1.SDA, J1.pin1
  N10: LCD2004-I2C1.SCL, J1.pin2
  N11: ZS-042_RTC1.GND, J3.pin1
  N12: ZS-042_RTC1.VCC, J3.pin2
  N13: ZS-042_RTC1.SDA, J4.pin1
  N14: ZS-042_RTC1.SCL, J4.pin2
  N15: microSD1.GND, J5.pin1
  N16: microSD1.VCC, J5.pin2
  N17: Mod1.GND, Mod1.-, J7.pin2
  N18: Mod1.+, J7.pin1
  N19: Part2.VCC, J6.pin1
  N20: Part2.GND, J6.pin2

custom parts:
  LCD2004-I2C: A standard character display with 4x20 characters. Comes in many colors with LCM2004 IIC attached.
  18650 battery holder: 18650 Battery Holder
  ACS712 Current Sensor 5A 20A 30A: Remix by Michael Kubina http://www.kubina.info Original by: https://forum.fritzing.org/t/current-sensor-5a-acs712/7694 https://forum.fritzing.org/u/ArtHome ArtHome12@gmail.com
